// Logisim project task1.circ as structural Verilog: 1 circuit, main circuit main
module main (
  input  \А ,
  input  B,
  input  C,
  input  [7:0] in_4,
  input  [7:0] in_5,
  input  C1,
  input  [3:0] a_b_c_d,
  output out_8,
  output out_9,
  output [7:0] out_10,
  output out_11,
  output out_12,
  output out_13,
  output out_14,
  output out_15,
  output out_16,
  output out_17,
  output out_18,
  output out_19,
  output out_20,
  output out_21,
  output out_22,
  output out_23,
  output out_24,
  output out_25,
  output out_26,
  output [3:0] out_27
);

  wire _2_2_out, _2_3_out, _2_4_out, _2_5_out, _2_6_out, _2_7_out, _2_8_out, _2_9_out, _2_out, _21_2_out,
       _21_3_out, _21_4_out, _21_5_out, _21_6_out, _21_7_out, _21_8_out, _21_9_out, _21_out, and_2_out,
       and_3_out, and_4_out, and_5_out, and_7_out, and_9_out, and_10_out, and_11_out, and_12_out, and_13_out,
       and_14_out, and_15_out, and_16_out, and_17_out, and_18_out, and_19_out, and_20_out, and_21_out,
       and_22_out, and_23_out, and_25_out, and_27_out, and_29_out, and_31_out, and_32_out, and_34_out,
       and_36_out, and_38_out, and_40_out, not_1_out, not_2_out, not_3_out, not_5_out, not_6_out, not_7_out,
       not_8_out, not_9_out, not_10_out, not_11_out, not_12_out, not_13_out, not_14_out, not_15_out,
       not_16_out, not_17_out, not_18_out, not_19_out, not_20_out, not_21_out, not_22_out, not_23_out,
       not_24_out, not_25_out, not_26_out, not_27_out, not_28_out, not_29_out, or_1_out, or_2_out, or_3_out,
       or_4_out, or_5_out, or_7_out, or_8_out, or_9_out, or_10_out, or_11_out, or_12_out, or_13_out,
       or_14_out, or_15_out, or_16_out, or_17_out, or_18_out, or_19_out, or_20_out, or_21_out, or_22_out,
       or_23_out, or_24_out, or_25_out, or_26_out, or_27_out, or_28_out, or_29_out, or_30_out, or_31_out,
       or_32_out, or_33_out, or_34_out, or_35_out, or_36_out, or_37_out, or_38_out, or_39_out, or_40_out,
       or_41_out, or_42_out, or_43_out, or_44_out, or_45_out, or_46_out, or_47_out, or_48_out, or_49_out,
       or_50_out, or_51_out, or_52_out, or_53_out, or_54_out, or_55_out, or_56_out, or_57_out, or_58_out,
       or_59_out, or_60_out, or_61_out, or_62_out, or_63_out, or_64_out, or_65_out, or_66_out, or_67_out,
       or_68_out, or_69_out, or_70_out, or_71_out, or_72_out, or_73_out;

  not not_1 (not_1_out, \А );
  not not_2 (not_2_out, B);
  not not_3 (not_3_out, C);
  or _2 (_2_out, C, not_2_out);
  or or_1 (or_1_out, \А , C);
  or or_2 (or_2_out, not_2_out, not_3_out);
  or or_3 (or_3_out, B, not_3_out);
  not not_4 (out_27[1], a_b_c_d[1]);
  or or_4 (or_4_out, B, C);
  not not_5 (not_5_out, a_b_c_d[2]);
  and and_1 (out_27[3], a_b_c_d[2], a_b_c_d[1]);
  or _21 (_21_out, \А , B);
  or or_5 (or_5_out, \А , or_4_out);
  and and_2 (and_2_out, a_b_c_d[1], not_5_out);
  and and_3 (and_3_out, out_27[1], a_b_c_d[2], a_b_c_d[2]);
  or or_6 (out_27[2], and_2_out, and_3_out);
  or or_7 (or_7_out, not_1_out, or_3_out);
  or or_8 (or_8_out, or_2_out, \А );
  not not_6 (not_6_out, in_4[0]);
  not not_7 (not_7_out, in_5[0]);
  not not_8 (not_8_out, C1);
  not not_9 (not_9_out, in_4[1]);
  not not_10 (not_10_out, in_5[1]);
  not not_11 (not_11_out, out_11);
  not not_12 (not_12_out, in_4[2]);
  not not_13 (not_13_out, in_5[2]);
  not not_14 (not_14_out, out_13);
  not not_15 (not_15_out, in_4[3]);
  not not_16 (not_16_out, in_5[3]);
  not not_17 (not_17_out, out_15);
  not not_18 (not_18_out, in_4[4]);
  not not_19 (not_19_out, in_5[4]);
  not not_20 (not_20_out, out_17);
  not not_21 (not_21_out, in_4[5]);
  not not_22 (not_22_out, in_5[5]);
  not not_23 (not_23_out, out_19);
  or or_9 (or_9_out, not_1_out, _2_out);
  or or_10 (or_10_out, in_4[0], C1);
  or _2_2 (_2_2_out, C1, not_7_out);
  or or_11 (or_11_out, not_7_out, not_8_out);
  or or_12 (or_12_out, in_5[0], not_8_out);
  or or_13 (or_13_out, in_4[1], out_11);
  or _2_3 (_2_3_out, out_11, not_10_out);
  or or_14 (or_14_out, not_10_out, not_11_out);
  or or_15 (or_15_out, in_5[1], not_11_out);
  or or_16 (or_16_out, in_4[2], out_13);
  or _2_4 (_2_4_out, out_13, not_13_out);
  or or_17 (or_17_out, not_13_out, not_14_out);
  or or_18 (or_18_out, in_5[2], not_14_out);
  or or_19 (or_19_out, in_4[3], out_15);
  or _2_5 (_2_5_out, out_15, not_16_out);
  or or_20 (or_20_out, not_16_out, not_17_out);
  or _2_6 (_2_6_out, out_17, not_19_out);
  or _2_7 (_2_7_out, out_19, not_22_out);
  not not_24 (not_24_out, in_4[6]);
  not not_25 (not_25_out, in_5[6]);
  not not_26 (not_26_out, out_21);
  not not_27 (not_27_out, in_4[7]);
  not not_28 (not_28_out, in_5[7]);
  not not_29 (not_29_out, out_23);
  and and_4 (and_4_out, or_1_out, or_4_out);
  and and_5 (and_5_out, or_9_out, or_8_out);
  or or_21 (or_21_out, in_5[0], C1);
  or or_22 (or_22_out, in_5[1], out_11);
  or or_23 (or_23_out, in_5[2], out_13);
  or or_24 (or_24_out, in_5[3], out_15);
  or or_25 (or_25_out, in_5[3], not_17_out);
  or or_26 (or_26_out, in_4[4], out_17);
  or or_27 (or_27_out, not_19_out, not_20_out);
  or or_28 (or_28_out, in_5[4], not_20_out);
  or or_29 (or_29_out, in_4[5], out_19);
  or or_30 (or_30_out, not_22_out, not_23_out);
  or or_31 (or_31_out, in_5[5], not_23_out);
  or or_32 (or_32_out, in_4[6], out_21);
  or _2_8 (_2_8_out, out_21, not_25_out);
  or or_33 (or_33_out, not_25_out, not_26_out);
  or or_34 (or_34_out, in_5[6], not_26_out);
  or _2_9 (_2_9_out, out_23, not_28_out);
  or _21_2 (_21_2_out, in_4[0], in_5[0]);
  or or_35 (or_35_out, in_4[0], or_21_out);
  or _21_3 (_21_3_out, in_4[1], in_5[1]);
  or or_36 (or_36_out, in_4[1], or_22_out);
  or _21_4 (_21_4_out, in_4[2], in_5[2]);
  or or_37 (or_37_out, in_4[2], or_23_out);
  or _21_5 (_21_5_out, in_4[3], in_5[3]);
  or or_38 (or_38_out, in_4[3], or_24_out);
  or _21_6 (_21_6_out, in_4[4], in_5[4]);
  or or_39 (or_39_out, in_5[4], out_17);
  or _21_7 (_21_7_out, in_4[5], in_5[5]);
  or or_40 (or_40_out, in_5[5], out_19);
  or or_41 (or_41_out, in_5[6], out_21);
  or or_42 (or_42_out, in_4[7], out_23);
  or or_43 (or_43_out, not_28_out, not_29_out);
  or or_44 (or_44_out, in_5[7], not_29_out);
  and and_6 (out_8, and_4_out, _21_out);
  and and_7 (and_7_out, and_5_out, or_7_out);
  or or_45 (or_45_out, in_4[4], or_39_out);
  or or_46 (or_46_out, in_4[5], or_40_out);
  or _21_8 (_21_8_out, in_4[6], in_5[6]);
  or or_47 (or_47_out, in_4[6], or_41_out);
  or _21_9 (_21_9_out, in_4[7], in_5[7]);
  or or_48 (or_48_out, in_5[7], out_23);
  or or_49 (or_49_out, in_4[7], or_48_out);
  and and_8 (out_9, or_5_out, and_7_out);
  or or_50 (or_50_out, not_6_out, or_12_out);
  or or_51 (or_51_out, not_9_out, or_15_out);
  or or_52 (or_52_out, not_12_out, or_18_out);
  or or_53 (or_53_out, not_15_out, or_25_out);
  or or_54 (or_54_out, not_18_out, or_28_out);
  or or_55 (or_55_out, not_21_out, or_31_out);
  or or_56 (or_56_out, or_11_out, in_4[0]);
  or or_57 (or_57_out, or_14_out, in_4[1]);
  or or_58 (or_58_out, or_17_out, in_4[2]);
  or or_59 (or_59_out, or_20_out, in_4[3]);
  or or_60 (or_60_out, or_27_out, in_4[4]);
  or or_61 (or_61_out, or_30_out, in_4[5]);
  or or_62 (or_62_out, not_24_out, or_34_out);
  or or_63 (or_63_out, not_27_out, or_44_out);
  or or_64 (or_64_out, not_6_out, _2_2_out);
  or or_65 (or_65_out, not_9_out, _2_3_out);
  or or_66 (or_66_out, not_12_out, _2_4_out);
  or or_67 (or_67_out, not_15_out, _2_5_out);
  or or_68 (or_68_out, or_33_out, in_4[6]);
  or or_69 (or_69_out, or_43_out, in_4[7]);
  and and_9 (and_9_out, or_10_out, or_21_out);
  and and_10 (and_10_out, or_64_out, or_56_out);
  and and_11 (and_11_out, or_13_out, or_22_out);
  and and_12 (and_12_out, or_65_out, or_57_out);
  and and_13 (and_13_out, or_16_out, or_23_out);
  and and_14 (and_14_out, or_66_out, or_58_out);
  and and_15 (and_15_out, or_19_out, or_24_out);
  and and_16 (and_16_out, or_26_out, or_39_out);
  or or_70 (or_70_out, not_18_out, _2_6_out);
  and and_17 (and_17_out, or_29_out, or_40_out);
  or or_71 (or_71_out, not_21_out, _2_7_out);
  or or_72 (or_72_out, not_24_out, _2_8_out);
  or or_73 (or_73_out, not_27_out, _2_9_out);
  and and_18 (and_18_out, or_67_out, or_59_out);
  and and_19 (and_19_out, or_70_out, or_60_out);
  and and_20 (and_20_out, or_71_out, or_61_out);
  and and_21 (and_21_out, or_32_out, or_41_out);
  and and_22 (and_22_out, or_72_out, or_68_out);
  and and_23 (and_23_out, or_42_out, or_48_out);
  and and_24 (out_11, and_9_out, _21_2_out);
  and and_25 (and_25_out, and_10_out, or_50_out);
  and and_26 (out_13, and_11_out, _21_3_out);
  and and_27 (and_27_out, and_12_out, or_51_out);
  and and_28 (out_15, and_13_out, _21_4_out);
  and and_29 (and_29_out, and_14_out, or_52_out);
  and and_30 (out_17, and_15_out, _21_5_out);
  and and_31 (and_31_out, or_73_out, or_69_out);
  and and_32 (and_32_out, and_18_out, or_53_out);
  and and_33 (out_19, and_16_out, _21_6_out);
  and and_34 (and_34_out, and_19_out, or_54_out);
  and and_35 (out_21, and_17_out, _21_7_out);
  and and_36 (and_36_out, and_20_out, or_55_out);
  and and_37 (out_23, and_21_out, _21_8_out);
  and and_38 (and_38_out, and_22_out, or_62_out);
  and and_39 (out_25, and_23_out, _21_9_out);
  and and_40 (and_40_out, and_31_out, or_63_out);
  and and_41 (out_10[0], or_35_out, and_25_out);
  and and_42 (out_10[1], or_36_out, and_27_out);
  and and_43 (out_10[2], or_37_out, and_29_out);
  and and_44 (out_10[3], or_38_out, and_32_out);
  and and_45 (out_10[4], or_45_out, and_34_out);
  and and_46 (out_10[5], or_46_out, and_36_out);
  and and_47 (out_10[6], or_47_out, and_38_out);
  and and_48 (out_10[7], or_49_out, and_40_out);

  assign out_12 = out_10[0];
  assign out_14 = out_10[1];
  assign out_16 = out_10[2];
  assign out_18 = out_10[3];
  assign out_20 = out_10[4];
  assign out_22 = out_10[5];
  assign out_24 = out_10[6];
  assign out_26 = out_10[7];
  assign out_27[0] = a_b_c_d[0];

  // Notes on the sheet:
  //   3
  //   1
  //   5
  //   A
  //   B
  //   18
  //   7
  //   11
  //   4
  //   1
  //   2
  //   16
  //   15
  //   3
  //   5
  //   13
  //   А1
  //   B1
  //   C1
  //   А2
  //   B2
  //   C2
  //   А3
  //   B3
  //   C3
  //   А4
  //   B4
  //   C4
  //   8
  //   3
  //   1
  //   5
  //   3
  //   1
  //   5
  //   3
  //   1
  //   5
  //   3
  //   А5
  //   B5
  //   C5
  //   А6
  //   B6
  //   C6
  //   А7
  //   B7
  //   C7
  //   4
  //   1
  //   5
  //   3
  //   1
  //   5
  //   3
  //   1
  //   5
  //   3
  //   1
  //   5
  //   А8
  //   B8
  //   C8
  //   20
  //   18
  //   7
  //   11
  //   18
  //   7
  //   11
  //   18
  //   7
  //   11
  //   18
  //   7
  //   11
  //   3
  //   1
  //   5
  //   9
  //   15
  //   15
  //   15
  //   15
  //   18
  //   7
  //   11
  //   18
  //   7
  //   11
  //   18
  //   7
  //   11
  //   16
  //   16
  //   16
  //   16
  //   16
  //   15
  //   16
  //   15
  //   15
  //   18
  //   15
  //   7
  //   11
  //   22
  //   14
  //   16
  //   16
  //   P
  //   13
  //   13
  //   13
  //   13
  //   17
  //   13
  //   13
  //   13
  //   S
  //   8
  //   8
  //   8
  //   8
  //   8
  //   8
  //   13
  //   4
  //   4
  //   4
  //   4
  //   4
  //   4
  //   8
  //   8
  //   20
  //   9
  //   20
  //   9
  //   20
  //   9
  //   20
  //   9
  //   20
  //   20
  //   4
  //   4
  //   9
  //   9
  //   20
  //   9
  //   20
  //   22
  //   14
  //   22
  //   14
  //   22
  //   14
  //   22
  //   14
  //   9
  //   22
  //   14
  //   22
  //   14
  //   22
  //   14
  //   P1
  //   17
  //   P2
  //   17
  //   P3
  //   17
  //   P4
  //   17
  //   P5
  //   P6
  //   22
  //   14
  //   17
  //   17
  //   P7
  //   17
  //   P8
  //   S1
  //   S2
  //   S3
  //   S4
  //   S5
  //   S6
  //   17
  //   S7
  //   S8
endmodule
